// Logisim project KIOURT_MECHMETALI_ACHMET_1084672.circ as structural Verilog: 1 circuit, main circuit main
module main (
  input  CLEAR,
  input  PRESET,
  input  in_3
);

  wire CLK_out, n7408_1_pin3, n7408_1_pin6, n7408_1_pin11, n7408_1_pin13, n7408_3_pin3, n7408_3_pin5,
       n7408_3_pin8, n7408_3_pin11, n7408_4_pin3, n7411_1_pin1, n7411_1_pin2, n7411_1_pin12, n7411_1_pin13,
       n7432_1_p3, n7432_1_p4, n7432_2_pin8, n7432_2_pin9, n7432_2_pin10, n7474_1_pin2, n7474_1_pin5,
       n7474_1_pin9, n7474_1_pin12, n7474_2_pin2, sevensegdec_1_p1, sevensegdec_1_p6, sevensegdec_1_p7,
       sevensegdec_1_p8, sevensegdec_1_p9, sevensegdec_1_p10, sevensegdec_1_p11, sevensegdec_1_p12;

  Clock CLK (.out(CLK_out));
  _7411 #(.ShowInternalStructure("true")) u_7411_1 (
    .pin1(n7411_1_pin1), .pin2(n7411_1_pin2), .pin13(n7411_1_pin13), .pin12(n7411_1_pin12));  // open: pin3, pin4, pin5, pin6, pin11, pin10, pin9, pin8
  _7474 #(.ShowInternalStructure("true")) u_7474_1 (
    .pin1(CLEAR), .pin2(n7474_1_pin2), .pin3(CLK_out), .pin4(PRESET), .pin5(n7474_1_pin5),
    .pin6(n7411_1_pin2), .pin13(CLEAR), .pin12(n7474_1_pin12), .pin11(CLK_out), .pin10(PRESET),
    .pin9(n7474_1_pin9), .pin8(n7411_1_pin13));
  // _7432 #(.ShowInternalStructure("true")) 7432_1: pin names not known; wires that end beside it: 1'b1, n7411_1_pin12, n7432_1_p3, n7432_1_p4, 1'b0
  _7408 #(.ShowInternalStructure("true")) u_7408_1 (
    .pin1(n7411_1_pin2), .pin2(n7411_1_pin13), .pin3(n7408_1_pin3), .pin4(n7411_1_pin1),
    .pin5(n7411_1_pin13), .pin6(n7408_1_pin6), .pin13(n7408_1_pin13), .pin12(n7411_1_pin13),
    .pin11(n7408_1_pin11));  // open: pin10, pin9, pin8
  // _7408 #(.ShowInternalStructure("true")) 7408_2: pin names not known; wires that end beside it: 1'b1, n7474_1_pin5, n7474_1_pin9, n7432_1_p3, 1'b0
  _7408 #(.ShowInternalStructure("true")) u_7408_3 (
    .pin1(n7411_1_pin1), .pin2(n7474_1_pin9), .pin3(n7408_3_pin3), .pin4(n7411_1_pin2), .pin5(n7408_3_pin5),
    .pin6(n7408_1_pin13), .pin13(n7408_3_pin5), .pin12(n7474_1_pin9), .pin11(n7408_3_pin11),
    .pin10(n7474_1_pin5), .pin9(n7411_1_pin1), .pin8(n7408_3_pin8));
  _7474 #(.ShowInternalStructure("true")) u_7474_2 (
    .pin1(CLEAR), .pin2(n7474_2_pin2), .pin3(CLK_out), .pin4(PRESET), .pin5(n7408_3_pin5), .pin6(n7411_1_pin1));  // open: pin13, pin12, pin11, pin10, pin9, pin8
  _7432 #(.ShowInternalStructure("true")) u_7432_2 (
    .pin1(n7408_3_pin3), .pin2(n7408_1_pin11), .pin3(n7474_2_pin2), .pin4(n7408_1_pin3), .pin5(n7408_1_pin6),
    .pin6(n7474_1_pin12), .pin13(n7408_3_pin11), .pin12(n7408_3_pin8), .pin11(n7474_1_pin2),
    .pin10(n7432_2_pin10), .pin9(n7432_2_pin9), .pin8(n7432_2_pin8));
  // SevenSegDec sevensegdec_1: pin names not known; wires that end beside it: sevensegdec_1_p1, n7432_2_pin8, n7474_1_pin5, n7432_1_p4, 1'b0, sevensegdec_1_p6, sevensegdec_1_p7, sevensegdec_1_p8, sevensegdec_1_p9, sevensegdec_1_p10, sevensegdec_1_p11, sevensegdec_1_p12
  _7_Segment_Display u_7_segment_display_1 (
    .g(sevensegdec_1_p12), .f(sevensegdec_1_p11), .a(sevensegdec_1_p6), .b(sevensegdec_1_p7),
    .e(sevensegdec_1_p10), .d(sevensegdec_1_p9), .c(sevensegdec_1_p8));  // open: dp
  _7408 #(.ShowInternalStructure("true")) u_7408_4 (
    .pin1(n7411_1_pin2), .pin2(n7408_3_pin5), .pin3(n7408_4_pin3), .pin4(n7408_4_pin3), .pin5(n7411_1_pin13),
    .pin6(sevensegdec_1_p1), .pin13(n7408_3_pin5), .pin12(n7474_1_pin9), .pin11(n7432_2_pin10),
    .pin10(n7474_1_pin5), .pin9(n7411_1_pin1), .pin8(n7432_2_pin9));
  // Digital_Oscilloscope digital_oscilloscope_1: pin names not known; wires that end beside it: 1'b1, CLK_out, sevensegdec_1_p1, n7432_2_pin8, n7474_1_pin5, n7432_1_p4, in_3, 1'b0
endmodule
