// Logisim project xor_kai_2sinartisi.circ as structural Verilog: 1 circuit, main circuit main
module main (
  input  A,
  input  B,
  input  C,
  input  D,
  input  B1,
  input  D1,
  input  A1,
  input  C1
);

  wire n7402_1_pin1, n7402_1_pin4, n7402_1_pin10, n7402_1_pin12, n7402_1_pin13, n7486_1_pin1, n7486_1_pin2,
       n7486_1_pin3;

  LED led_1 (.in(n7402_1_pin13));
  _7402 #(.ShowInternalStructure("true")) u_7402_1 (
    .pin1(n7402_1_pin1), .pin2(B1), .pin3(D1), .pin4(n7402_1_pin4), .pin5(A1), .pin6(C1),
    .pin13(n7402_1_pin13), .pin12(n7402_1_pin12), .pin11(n7402_1_pin12), .pin10(n7402_1_pin10), .pin9(B1),
    .pin8(C1));
  _7486 #(.ShowInternalStructure("true")) u_7486_1 (
    .pin1(n7486_1_pin1), .pin2(n7486_1_pin2), .pin3(n7486_1_pin3), .pin13(A), .pin12(B),
    .pin11(n7486_1_pin1), .pin10(C), .pin9(D), .pin8(n7486_1_pin2));  // open: pin4, pin5, pin6
  LED led_2 (.in(n7486_1_pin3));
  _7427 #(.ShowInternalStructure("true")) u_7427_1 (
    .pin1(n7402_1_pin4), .pin2(n7402_1_pin1), .pin13(n7402_1_pin10), .pin12(n7402_1_pin12));  // open: pin3, pin4, pin5, pin6, pin11, pin10, pin9, pin8
endmodule
