// Logisim project ALU.circ as structural Verilog: 3 circuits, main circuit ALU
module ALU (
  input  in_1,
  input  in_2,
  input  [3:0] A,
  input  [3:0] B,
  output Less,
  output Great,
  output Equal
);

  wire l_74181_1_p14, l_74181_1_p15, l_74181_1_p16, l_74181_1_p17, n7402_1_pin13, n7432_1_pin3, n7432_1_pin8,
       n7432_1_pin11;

  // L_74181 l_74181_1: pin names not known; wires that end beside it: in_2, in_2, in_1, in_1, B[3], A[3], B[2], A[2], B[1], A[1], B[0], A[0], Less, l_74181_1_p14, l_74181_1_p15, l_74181_1_p16, l_74181_1_p17
  _7432 #(.ShowInternalStructure("true")) u_7432_1 (
    .pin1(l_74181_1_p17), .pin2(l_74181_1_p16), .pin3(n7432_1_pin3), .pin13(l_74181_1_p15),
    .pin12(l_74181_1_p14), .pin11(n7432_1_pin11), .pin10(n7432_1_pin3), .pin9(n7432_1_pin11),
    .pin8(n7432_1_pin8));  // open: pin4, pin5, pin6
  _7402 #(.ShowInternalStructure("true")) u_7402_1 (
    .pin1(Equal), .pin2(n7432_1_pin8), .pin3(Less), .pin13(n7402_1_pin13), .pin12(n7432_1_pin8),
    .pin11(n7432_1_pin8), .pin10(Great), .pin9(n7402_1_pin13), .pin8(Less));  // open: pin4, pin5, pin6
endmodule

module ASKISI22 (
  input  Cn,
  input  X3,
  input  X2,
  input  X1,
  input  F3,
  input  F2,
  input  F1,
  input  F0,
  output aEQUALb,
  output aGREATb,
  output aLESSb,
  output Cn4
);

  wire n7404_1_pin2, n7404_1_pin4, n7404_1_pin6, n7404_1_pin12, n7404_2_pin2, n7404_2_pin4, n7404_2_pin10,
       n7404_2_pin12, n7404_3_pin2, n7404_3_pin4, n7404_3_pin10, n7404_3_pin12, n7408_1_pin3, n7408_1_pin6,
       n7408_1_pin8, n7408_1_pin11, n7408_2_pin3, n7408_2_pin6, n7408_2_pin8, n7408_2_pin11, n7408_3_pin3,
       n7408_3_pin5, n7432_1_pin3, n7432_1_pin11, n7432_2_pin4, n7432_2_pin5, n7486_1_pin3, n7486_1_pin6,
       n7486_1_pin8, n7486_1_pin11;

  _7486 #(.ShowInternalStructure("true")) u_7486_1 (
    .pin1(Cn), .pin2(Cn), .pin3(n7486_1_pin3), .pin4(Cn), .pin5(Cn), .pin6(n7486_1_pin6), .pin13(Cn),
    .pin12(Cn), .pin11(n7486_1_pin11), .pin10(Cn), .pin9(Cn), .pin8(n7486_1_pin8));
  _7404 #(.ShowInternalStructure("true")) u_7404_1 (
    .pin1(Cn), .pin2(n7404_1_pin2), .pin3(Cn), .pin4(n7404_1_pin4), .pin5(Cn), .pin6(n7404_1_pin6),
    .pin13(Cn), .pin12(n7404_1_pin12));  // open: pin11, pin10, pin9, pin8
  _7404 #(.ShowInternalStructure("true")) u_7404_2 (
    .pin1(Cn), .pin2(n7404_2_pin2), .pin3(Cn), .pin4(n7404_2_pin4), .pin13(Cn), .pin12(n7404_2_pin12),
    .pin11(Cn), .pin10(n7404_2_pin10));  // open: pin5, pin6, pin9, pin8
  _7404 #(.ShowInternalStructure("true")) u_7404_3 (
    .pin1(n7486_1_pin3), .pin2(n7404_3_pin2), .pin3(n7486_1_pin6), .pin4(n7404_3_pin4),
    .pin13(n7486_1_pin11), .pin12(n7404_3_pin12), .pin11(n7486_1_pin8), .pin10(n7404_3_pin10));  // open: pin5, pin6, pin9, pin8
  _7408 #(.ShowInternalStructure("true")) u_7408_1 (
    .pin1(Cn), .pin2(n7404_1_pin4), .pin3(n7408_1_pin3), .pin4(Cn), .pin5(n7404_1_pin6), .pin6(n7408_1_pin6),
    .pin13(Cn), .pin12(n7404_1_pin12), .pin11(n7408_1_pin11), .pin10(Cn), .pin9(n7404_1_pin2),
    .pin8(n7408_1_pin8));
  _7408 #(.ShowInternalStructure("true")) u_7408_2 (
    .pin1(n7404_2_pin10), .pin2(Cn), .pin3(n7408_2_pin3), .pin4(n7404_2_pin2), .pin5(Cn),
    .pin6(n7408_2_pin6), .pin13(n7404_2_pin12), .pin12(Cn), .pin11(n7408_2_pin11), .pin10(n7404_2_pin4),
    .pin9(Cn), .pin8(n7408_2_pin8));
  _7400 #(.ShowInternalStructure("true")) u_7400_1 (
    .pin13(Cn), .pin12(Cn), .pin11(Cn4));  // open: pin1, pin2, pin3, pin4, pin5, pin6, pin10, pin9, pin8
  _7408 #(.ShowInternalStructure("true")) u_7408_3 (
    .pin1(n7404_3_pin2), .pin2(n7404_3_pin4), .pin3(n7408_3_pin3), .pin4(n7408_3_pin3), .pin5(n7408_3_pin5),
    .pin6(aEQUALb), .pin13(n7404_3_pin12), .pin12(n7404_3_pin10), .pin11(n7408_3_pin5));  // open: pin10, pin9, pin8
  _7432 #(.ShowInternalStructure("true")) u_7432_1 (
    .pin1(n7408_1_pin3), .pin2(n7408_1_pin6), .pin3(n7432_1_pin3), .pin13(n7408_1_pin11),
    .pin12(n7408_1_pin8), .pin11(n7432_1_pin11), .pin10(n7432_1_pin11), .pin9(n7432_1_pin3), .pin8(aGREATb));  // open: pin4, pin5, pin6
  _7432 #(.ShowInternalStructure("true")) u_7432_2 (
    .pin4(n7432_2_pin4), .pin5(n7432_2_pin5), .pin6(aLESSb), .pin13(n7408_2_pin11), .pin12(n7408_2_pin3),
    .pin11(n7432_2_pin4), .pin10(n7408_2_pin6), .pin9(n7408_2_pin8), .pin8(n7432_2_pin5));  // open: pin1, pin2, pin3

  assign F0 = Cn;
  assign F1 = Cn;
  assign F2 = Cn;
  assign F3 = Cn;
  assign X1 = Cn;
  assign X2 = Cn;
  assign X3 = Cn;
endmodule

module Compare (
  input  F3,
  input  F2,
  input  F1,
  input  F0
);

  _7404 #(.ShowInternalStructure("true")) u_7404_1 ();  // open: pin1, pin2, pin3, pin4, pin5, pin6, pin13, pin12, pin11, pin10, pin9, pin8
endmodule
