// Logisim project ALUwemade.circ as structural Verilog: 1 circuit, main circuit main
module main (
  input  [3:0] S,
  input  [3:0] A,
  input  [3:0] B,
  input  [1:0] in_4
);

  wire l_74181_1_p15, l_74181_1_p16, l_74181_1_p17, l_74181_1_p18, l_74181_1_p19;

  // L_74181 l_74181_1: pin names not known; wires that end beside it: S[3], S[2], S[1], S[0], B[3], A[3], B[2], A[2], B[1], A[1], B[0], A[0], in_4[1], in_4[0], l_74181_1_p15, l_74181_1_p16, l_74181_1_p17, l_74181_1_p18, l_74181_1_p19
  LED led_1 (.in(l_74181_1_p15));
  LED led_2 (.in(l_74181_1_p16));
  LED led_3 (.in(l_74181_1_p17));
  LED led_4 (.in(l_74181_1_p18));
  LED led_5 (.in(l_74181_1_p19));
endmodule
