// Logisim project FLIPFLOPASKISI3B.circ as structural Verilog: 1 circuit, main circuit main
module main (
  input  in_1,
  input  Reset,
  input  in_3,
  input  in_4
);

  wire Clock1Hz_out, l_74181_1_p15, l_74181_1_p16, n7474_1_pin2, n7474_1_pin5;

  Clock Clock1Hz (.out(Clock1Hz_out));
  _7474 #(.ShowInternalStructure("true")) u_7474_1 (
    .pin1(in_1), .pin2(n7474_1_pin2), .pin3(Clock1Hz_out), .pin4(Reset), .pin5(n7474_1_pin5),
    .pin6(n7474_1_pin2));  // open: pin13, pin12, pin11, pin10, pin9, pin8
  // L_74181 l_74181_1: pin names not known; wires that end beside it: in_3, in_4, in_4, in_3, in_4, in_4, in_4, in_4, in_4, in_4, Clock1Hz_out, n7474_1_pin5, in_4, in_3, l_74181_1_p15, l_74181_1_p16
  // Digital_Oscilloscope digital_oscilloscope_1: pin names not known; wires that end beside it: 1'b0, Clock1Hz_out, n7474_1_pin5, l_74181_1_p15, l_74181_1_p16
endmodule
