// Logisim project KIOURT-MECHMETALI_ACHMET_1084672_ASKHSH6_logisim.circ as structural Verilog: 5 circuits, main circuit ASKHSH6_1
module ASKHSH6_1 (
  input  in_1,
  input  nCLR,
  input  D1,
  input  PRESET
);

  wire CLK_out, Dff1_Dff4_pin5, Dff1_Dff4_pin9, Dff1_Dff4_pin12, Dff2_Dff3_pin5;

  Clock CLK (.out(CLK_out));
  _7474 #(.ShowInternalStructure("true")) Dff1_Dff4 (
    .pin1(nCLR), .pin2(D1), .pin3(CLK_out), .pin4(PRESET), .pin5(Dff1_Dff4_pin5), .pin13(nCLR),
    .pin12(Dff1_Dff4_pin12), .pin11(CLK_out), .pin10(PRESET), .pin9(Dff1_Dff4_pin9));  // open: pin6, pin8
  _7474 #(.ShowInternalStructure("true")) Dff2_Dff3 (
    .pin1(nCLR), .pin2(Dff1_Dff4_pin5), .pin3(CLK_out), .pin4(PRESET), .pin5(Dff2_Dff3_pin5), .pin13(nCLR),
    .pin12(Dff2_Dff3_pin5), .pin11(CLK_out), .pin10(PRESET), .pin9(Dff1_Dff4_pin12));  // open: pin6, pin8
  // Digital_Oscilloscope #(.nState(8)) digital_oscilloscope_1: pin names not known; wires that end beside it: 1'b0, CLK_out, Dff1_Dff4_pin5, Dff2_Dff3_pin5, Dff1_Dff4_pin12, Dff1_Dff4_pin9, in_1
endmodule

module ASKHSH6_2 (
  input  in_1,
  input  nCLR,
  input  nPRE
);

  wire Dff1_Dff4_pin2, Dff1_Dff4_pin3, Dff1_Dff4_pin5, Dff1_Dff4_pin12, Dff2_Dff3_pin5;

  _7474 #(.ShowInternalStructure("true")) Dff1_Dff4 (
    .pin1(nCLR), .pin2(Dff1_Dff4_pin2), .pin3(Dff1_Dff4_pin3), .pin4(nPRE), .pin5(Dff1_Dff4_pin5),
    .pin13(nPRE), .pin12(Dff1_Dff4_pin12), .pin11(Dff1_Dff4_pin3), .pin10(nCLR), .pin9(Dff1_Dff4_pin2));  // open: pin6, pin8
  Clock clock_1 (.out(Dff1_Dff4_pin3));
  _7474 #(.ShowInternalStructure("true")) Dff2_Dff3 (
    .pin1(nCLR), .pin2(Dff1_Dff4_pin5), .pin3(Dff1_Dff4_pin3), .pin4(nPRE), .pin5(Dff2_Dff3_pin5),
    .pin13(nCLR), .pin12(Dff2_Dff3_pin5), .pin11(Dff1_Dff4_pin3), .pin10(nPRE), .pin9(Dff1_Dff4_pin12));  // open: pin6, pin8
  // Digital_Oscilloscope #(.nState(8)) digital_oscilloscope_1: pin names not known; wires that end beside it: 1'b0, Dff1_Dff4_pin3, Dff1_Dff4_pin5, Dff2_Dff3_pin5, Dff1_Dff4_pin12, Dff1_Dff4_pin2, in_1
endmodule

module ASKHSH6_3 (
  input  Clear,
  input  nCLR,
  input  nPRE
);

  wire Dff1_Dff4_pin2, Dff1_Dff4_pin3, Dff1_Dff4_pin5, Dff1_Dff4_pin9, Dff1_Dff4_pin12, Dff2_Dff3_pin5;

  _7474 #(.ShowInternalStructure("true")) Dff1_Dff4 (
    .pin1(nCLR), .pin2(Dff1_Dff4_pin2), .pin3(Dff1_Dff4_pin3), .pin4(nPRE), .pin5(Dff1_Dff4_pin5),
    .pin13(nPRE), .pin12(Dff1_Dff4_pin12), .pin11(Dff1_Dff4_pin3), .pin10(nCLR), .pin9(Dff1_Dff4_pin9));  // open: pin6, pin8
  Clock CLK (.out(Dff1_Dff4_pin3));
  _7474 #(.ShowInternalStructure("true")) Dff2_Dff3 (
    .pin1(nCLR), .pin2(Dff1_Dff4_pin5), .pin3(Dff1_Dff4_pin3), .pin4(nPRE), .pin5(Dff2_Dff3_pin5),
    .pin13(nCLR), .pin12(Dff2_Dff3_pin5), .pin11(Dff1_Dff4_pin3), .pin10(nPRE), .pin9(Dff1_Dff4_pin12));  // open: pin6, pin8
  _7486 #(.ShowInternalStructure("true")) u_7486_1 (
    .pin13(Dff1_Dff4_pin12), .pin12(Dff1_Dff4_pin9), .pin11(Dff1_Dff4_pin2));  // open: pin1, pin2, pin3, pin4, pin5, pin6, pin10, pin9, pin8
  // Digital_Oscilloscope #(.nState(8)) digital_oscilloscope_1: pin names not known; wires that end beside it: 1'b0, Dff1_Dff4_pin3, Dff1_Dff4_pin5, Dff2_Dff3_pin5, Dff1_Dff4_pin12, Dff1_Dff4_pin9, Clear
endmodule

module ASKHSH6_4 (
  input  nPRE,
  input  CLEAR,
  input  CLK,
  input  S0,
  input  S1,
  input  ln3,
  input  ln2,
  input  ln1,
  input  ln0,
  input  SHR,
  input  SHL,
  output Q3,
  output Q2,
  output Q1,
  output Q0
);

  wire n7474_1_pin2, n7474_1_pin12, n7474_2_pin2, n7474_2_pin12;

  _7474 #(.ShowInternalStructure("true")) u_7474_1 (
    .pin1(CLEAR), .pin2(n7474_1_pin2), .pin3(CLK), .pin4(nPRE), .pin5(Q2), .pin13(CLEAR),
    .pin12(n7474_1_pin12), .pin11(CLK), .pin10(nPRE), .pin9(Q3));  // open: pin6, pin8
  _7474 #(.ShowInternalStructure("true")) u_7474_2 (
    .pin1(CLEAR), .pin2(n7474_2_pin2), .pin3(CLK), .pin4(nPRE), .pin5(Q0), .pin13(CLEAR),
    .pin12(n7474_2_pin12), .pin11(CLK), .pin10(nPRE), .pin9(Q1));  // open: pin6, pin8
endmodule

module ASKHSH6_5 (
  input  PRESET,
  input  nCLR,
  input  CLK,
  input  S0,
  input  S1,
  input  A3,
  input  A2,
  input  A1,
  input  A0,
  input  B3,
  input  B2,
  input  B1,
  input  B0
);

  wire askhsh6_4_1_q0, askhsh6_4_1_q1, askhsh6_4_1_q2, askhsh6_4_1_q3, n74283_1_pin1, n74283_1_pin4,
       n74283_1_pin6, n74283_1_pin7;

  ASKHSH6_4 askhsh6_4_1 (
    .nPRE(PRESET), .CLEAR(nCLR), .CLK(CLK), .S0(S0), .S1(S1), .ln3(A3), .ln2(A2), .ln1(A1), .ln0(A0),
    .SHR(n74283_1_pin4), .Q3(askhsh6_4_1_q3), .Q2(askhsh6_4_1_q2), .Q1(askhsh6_4_1_q1), .Q0(askhsh6_4_1_q0));  // open: SHL
  _74283 #(.ShowInternalStructure("true")) u_74283_1 (
    .pin1(n74283_1_pin1), .pin4(n74283_1_pin4), .pin5(askhsh6_4_1_q0), .pin6(n74283_1_pin6),
    .pin7(n74283_1_pin7), .pin12(askhsh6_4_1_q3));  // open: pin2, pin3, pin15, pin14, pin13, pin11, pin10, pin9
  ASKHSH6_4 askhsh6_4_2 (
    .nPRE(PRESET), .CLEAR(nCLR), .CLK(CLK), .S0(S0), .S1(S1), .ln3(B3), .ln2(B2), .ln1(B1), .ln0(B0),
    .Q0(n74283_1_pin6));  // open: SHR, SHL, Q3, Q2, Q1
  LED led_1 (.in(askhsh6_4_1_q3));
  LED led_2 (.in(askhsh6_4_1_q2));
  LED led_3 (.in(askhsh6_4_1_q1));
  LED led_4 (.in(askhsh6_4_1_q0));
  _7474 #(.ShowInternalStructure("true")) u_7474_1 (
    .pin1(nCLR), .pin2(n74283_1_pin1), .pin3(CLK), .pin4(PRESET), .pin5(n74283_1_pin7));  // open: pin6, pin13, pin12, pin11, pin10, pin9, pin8

  // Notes on the sheet:
  //   ΞΊΞ±Ο„Ξ±Ο‡Ο‰Ο�Ξ·Ο„Ξ®  A
  //   ΞΊΞ±Ο„Ξ±Ο‡Ο‰Ο�Ξ·Ο„Ξ® Ξ’
endmodule
