// Logisim project ASKHSH7.circ as structural Verilog: 4 circuits, main circuit ERWTHMA_A1a
module ERWTHMA_A1a (
  input  in_1,
  input  SET,
  input  JK,
  input  CLR
);

  wire CLK_out, l_74112_2_q2, n7408_1_pin1, n7408_1_pin2, n7408_1_pin3, n7408_1_pin4, n7408_1_pin6,
       sevensegdec_1_p1, sevensegdec_1_p2, sevensegdec_1_p3, sevensegdec_1_p4, sevensegdec_1_p5,
       sevensegdec_1_p6, sevensegdec_1_p7;

  Clock CLK (.out(CLK_out));
  _7408 #(.ShowInternalStructure("true")) u_7408_1 (
    .pin1(n7408_1_pin1), .pin2(n7408_1_pin2), .pin3(n7408_1_pin3), .pin4(n7408_1_pin4), .pin5(n7408_1_pin3),
    .pin6(n7408_1_pin6));  // open: pin13, pin12, pin11, pin10, pin9, pin8
  L_74112 l_74112_1 (
    .SET1(SET), .J1(JK), .K1(JK), .CLK1(CLK_out), .CLR1(CLR), .SET2(SET), .J2(n7408_1_pin1),
    .K2(n7408_1_pin1), .CLK2(CLK_out), .CLR2(CLR), .Q1(n7408_1_pin1), .Q2(n7408_1_pin2));  // open: Q1_N, Q2_N
  L_74112 l_74112_2 (
    .SET1(SET), .J1(n7408_1_pin3), .K1(n7408_1_pin3), .CLK1(CLK_out), .CLR1(CLR), .SET2(SET),
    .J2(n7408_1_pin6), .K2(n7408_1_pin6), .CLK2(CLK_out), .CLR2(CLR), .Q1(n7408_1_pin4), .Q2(l_74112_2_q2));  // open: Q1_N, Q2_N
  // Digital_Oscilloscope #(.nState(20)) digital_oscilloscope_1: pin names not known; wires that end beside it: l_74112_2_q2, n7408_1_pin4, n7408_1_pin2, n7408_1_pin1, CLK_out, l_74112_2_q2, n7408_1_pin4, n7408_1_pin2, n7408_1_pin1, in_1
  // SevenSegDec sevensegdec_1: pin names not known; wires that end beside it: sevensegdec_1_p1, sevensegdec_1_p2, sevensegdec_1_p3, sevensegdec_1_p4, sevensegdec_1_p5, sevensegdec_1_p6, sevensegdec_1_p7
  _7_Segment_Display u_7_segment_display_1 (
    .g(sevensegdec_1_p7), .f(sevensegdec_1_p6), .a(sevensegdec_1_p1), .b(sevensegdec_1_p2),
    .e(sevensegdec_1_p5), .d(sevensegdec_1_p4), .c(sevensegdec_1_p3));  // open: dp
endmodule

module ERWTHMA_A2 (
  input  UpDown,
  input  in_2,
  input  SET,
  input  JK,
  input  CLR
);

  wire CLK_out, l_74112_2_q2, n74266_1_pin2, n74266_1_pin3, n74266_1_pin5, n74266_1_pin6, n74266_1_pin8,
       n74266_1_pin9, sevensegdec_1_p4, sevensegdec_1_p5, sevensegdec_1_p6, sevensegdec_1_p7,
       sevensegdec_1_p8, sevensegdec_1_p9, sevensegdec_1_p10;

  Clock CLK (.out(CLK_out));
  _74266 #(.ShowInternalStructure("true")) u_74266_1 (
    .pin1(UpDown), .pin2(n74266_1_pin2), .pin3(n74266_1_pin3), .pin4(UpDown), .pin5(n74266_1_pin5),
    .pin6(n74266_1_pin6), .pin10(UpDown), .pin9(n74266_1_pin9), .pin8(n74266_1_pin8));  // open: pin13, pin12, pin11
  L_74112 l_74112_1 (
    .SET1(SET), .J1(JK), .K1(JK), .CLK1(CLK_out), .CLR1(CLR), .SET2(SET), .J2(JK), .K2(JK),
    .CLK2(n74266_1_pin3), .CLR2(CLR), .Q1(n74266_1_pin2), .Q2(n74266_1_pin5));  // open: Q1_N, Q2_N
  L_74112 l_74112_2 (
    .SET1(SET), .J1(JK), .K1(JK), .CLK1(n74266_1_pin6), .CLR1(CLR), .SET2(SET), .J2(JK), .K2(JK),
    .CLK2(n74266_1_pin8), .CLR2(CLR), .Q1(n74266_1_pin9), .Q2(l_74112_2_q2));  // open: Q1_N, Q2_N
  // Digital_Oscilloscope #(.nState(20)) digital_oscilloscope_1: pin names not known; wires that end beside it: CLK_out, l_74112_2_q2, n74266_1_pin9, n74266_1_pin5, n74266_1_pin2, in_2
  // SevenSegDec sevensegdec_1: pin names not known; wires that end beside it: n74266_1_pin9, n74266_1_pin5, n74266_1_pin2, sevensegdec_1_p4, sevensegdec_1_p5, sevensegdec_1_p6, sevensegdec_1_p7, sevensegdec_1_p8, sevensegdec_1_p9, sevensegdec_1_p10
  _7_Segment_Display u_7_segment_display_1 (
    .g(sevensegdec_1_p10), .f(sevensegdec_1_p9), .a(sevensegdec_1_p4), .b(sevensegdec_1_p5),
    .e(sevensegdec_1_p8), .d(sevensegdec_1_p7), .c(sevensegdec_1_p6));  // open: dp
endmodule

module ERWTHMA_A1b (
  input  enable,
  input  in_2,
  input  SET,
  input  CLR
);

  wire clock_1_out, digital_oscilloscope_1_p5, n7408_1_pin1, n7408_1_pin2, n7408_1_pin3, n7408_1_pin5,
       n7408_1_pin6, n7408_1_pin11, sevensegdec_1_p5, sevensegdec_1_p6, sevensegdec_1_p7, sevensegdec_1_p8,
       sevensegdec_1_p9, sevensegdec_1_p10, sevensegdec_1_p11;

  Clock clock_1 (.out(clock_1_out));
  _7408 #(.ShowInternalStructure("true")) u_7408_1 (
    .pin1(n7408_1_pin1), .pin2(n7408_1_pin2), .pin3(n7408_1_pin3), .pin4(n7408_1_pin3), .pin5(n7408_1_pin5),
    .pin6(n7408_1_pin6), .pin13(enable), .pin12(clock_1_out), .pin11(n7408_1_pin11));  // open: pin10, pin9, pin8
  L_74112 l_74112_1 (
    .SET1(SET), .J1(1'b1), .K1(1'b1), .CLK1(n7408_1_pin11), .CLR1(CLR), .SET2(SET), .J2(n7408_1_pin1),
    .K2(n7408_1_pin1), .CLK2(n7408_1_pin11), .CLR2(CLR), .Q1(n7408_1_pin1), .Q2(n7408_1_pin2));  // open: Q1_N, Q2_N
  // Digital_Oscilloscope #(.nState(20)) digital_oscilloscope_1: pin names not known; wires that end beside it: n7408_1_pin11, n7408_1_pin1, n7408_1_pin2, n7408_1_pin5, digital_oscilloscope_1_p5, in_2
  L_74112 l_74112_2 (
    .SET1(SET), .J1(n7408_1_pin3), .K1(n7408_1_pin3), .CLK1(n7408_1_pin11), .CLR1(CLR), .SET2(SET),
    .J2(n7408_1_pin6), .K2(n7408_1_pin6), .CLK2(n7408_1_pin11), .CLR2(CLR), .Q1(n7408_1_pin5),
    .Q2(digital_oscilloscope_1_p5));  // open: Q1_N, Q2_N
  // SevenSegDec sevensegdec_1: pin names not known; wires that end beside it: digital_oscilloscope_1_p5, n7408_1_pin5, n7408_1_pin2, n7408_1_pin1, sevensegdec_1_p5, sevensegdec_1_p6, sevensegdec_1_p7, sevensegdec_1_p8, sevensegdec_1_p9, sevensegdec_1_p10, sevensegdec_1_p11
  _7_Segment_Display u_7_segment_display_1 (
    .g(sevensegdec_1_p11), .f(sevensegdec_1_p10), .a(sevensegdec_1_p5), .b(sevensegdec_1_p6),
    .e(sevensegdec_1_p9), .d(sevensegdec_1_p8), .c(sevensegdec_1_p7));  // open: dp
endmodule

module ERWTHMA_B1 (
  input  LOAD,
  input  Enable,
  input  N3,
  input  N2,
  input  N1,
  input  N0
);

  wire CLK_out, n7400_1_pin3, n7400_1_pin6, n7400_1_pin8, n7400_1_pin11, n7400_2_pin3, n7400_2_pin6,
       n7400_2_pin8, n7400_2_pin11, n7402_1_pin1, n7402_1_pin4, n7402_1_pin10, n7402_1_pin11, n7402_1_pin13,
       n7402_2_pin1, n7402_2_pin13, n7408_1_pin1, n7408_1_pin2, n7408_1_pin3, n7408_1_pin5, n7408_1_pin6,
       n7408_1_pin8, n7408_1_pin11, n7408_1_pin13, sevensegdec_1_p5, sevensegdec_1_p6, sevensegdec_1_p7,
       sevensegdec_1_p8, sevensegdec_1_p9, sevensegdec_1_p10, sevensegdec_1_p11;

  Clock CLK (.out(CLK_out));
  _7408 #(.ShowInternalStructure("true")) u_7408_1 (
    .pin1(n7408_1_pin1), .pin2(n7408_1_pin2), .pin3(n7408_1_pin3), .pin4(n7408_1_pin3), .pin5(n7408_1_pin5),
    .pin6(n7408_1_pin6), .pin13(n7408_1_pin13), .pin12(Enable), .pin11(n7408_1_pin11), .pin10(Enable),
    .pin9(n7408_1_pin2), .pin8(n7408_1_pin8));
  _7400 #(.ShowInternalStructure("true")) u_7400_1 (
    .pin1(N1), .pin2(N3), .pin3(n7400_1_pin3), .pin4(n7400_1_pin3), .pin5(N3), .pin6(n7400_1_pin6),
    .pin13(N0), .pin12(N3), .pin11(n7400_1_pin11), .pin10(n7400_1_pin11), .pin9(N3), .pin8(n7400_1_pin8));
  L_74112 l_74112_1 (
    .SET1(n7400_1_pin3), .J1(n7408_1_pin8), .K1(n7408_1_pin8), .CLK1(CLK_out), .CLR1(n7400_1_pin6),
    .SET2(n7400_1_pin11), .J2(n7408_1_pin11), .K2(n7408_1_pin11), .CLK2(CLK_out), .CLR2(n7400_1_pin8),
    .Q1(n7408_1_pin1), .Q2(n7408_1_pin2));  // open: Q1_N, Q2_N
  _7402 #(.ShowInternalStructure("true")) u_7402_1 (
    .pin1(n7402_1_pin1), .pin2(n7408_1_pin2), .pin3(n7408_1_pin1), .pin4(n7402_1_pin4), .pin5(n7402_1_pin1),
    .pin6(n7402_1_pin1), .pin13(n7402_1_pin13), .pin12(n7408_1_pin5), .pin11(n7402_1_pin11),
    .pin10(n7402_1_pin10), .pin9(n7402_1_pin13), .pin8(n7402_1_pin13));
  _7400 #(.ShowInternalStructure("true")) u_7400_2 (
    .pin1(N3), .pin2(N3), .pin3(n7400_2_pin3), .pin4(n7400_2_pin3), .pin5(N3), .pin6(n7400_2_pin6),
    .pin13(N2), .pin12(N3), .pin11(n7400_2_pin11), .pin10(n7400_2_pin11), .pin9(N3), .pin8(n7400_2_pin8));
  _7402 #(.ShowInternalStructure("true")) u_7402_2 (
    .pin1(n7402_2_pin1), .pin2(n7402_1_pin4), .pin3(n7402_1_pin10), .pin13(n7402_2_pin13),
    .pin12(n7402_2_pin1), .pin11(LOAD), .pin10(N3), .pin9(n7402_2_pin13), .pin8(n7402_2_pin13));  // open: pin4, pin5, pin6
  L_74112 l_74112_2 (
    .SET1(n7400_2_pin3), .J1(n7408_1_pin6), .K1(n7408_1_pin6), .CLK1(CLK_out), .CLR1(n7400_2_pin6),
    .SET2(n7400_2_pin11), .J2(n7408_1_pin3), .K2(n7408_1_pin3), .CLK2(CLK_out), .CLR2(n7400_2_pin8),
    .Q1(n7402_1_pin11), .Q2(n7408_1_pin5));  // open: Q1_N, Q2_N
  // SevenSegDec sevensegdec_1: pin names not known; wires that end beside it: n7402_1_pin11, n7408_1_pin5, n7408_1_pin1, n7408_1_pin2, sevensegdec_1_p5, sevensegdec_1_p6, sevensegdec_1_p7, sevensegdec_1_p8, sevensegdec_1_p9, sevensegdec_1_p10, sevensegdec_1_p11
  _7_Segment_Display u_7_segment_display_1 (
    .g(sevensegdec_1_p11), .f(sevensegdec_1_p10), .a(sevensegdec_1_p5), .b(sevensegdec_1_p6),
    .e(sevensegdec_1_p9), .d(sevensegdec_1_p8), .c(sevensegdec_1_p7));  // open: dp
  // also tied to VCC on the sheet: n7408_1_pin13

  // Notes on the sheet:
  //   JKff1 and JKff0
  //   JKff3 and JKff2
endmodule
